// Logisim project NEW_dual_port_ram.circ as structural Verilog: 2 circuits, main circuit memoria
module memoria (
  output [7:0] out_1,
  output [7:0] out_2
);

  wire and_1_out, button_1_out, clock_1_out;
  wire [7:0] adder_1_out, register_1_q;

  Register register_1 (.D(adder_1_out), .en(1'b1), .clk(clock_1_out), .Q(register_1_q), .clr(button_1_out));
  Adder adder_1 (.a(register_1_q), .b(8'h1), .out(adder_1_out), .cin(1'b0));  // open: cout
  Clock #(.highDuration(2), .lowDuration(2)) clock_1 (.out(clock_1_out));
  Button button_1 (.out(button_1_out));
  and and_1 (and_1_out, out_1[0], out_1[1]);
  dual_port_ram dual_port_ram_1 (
    .addr({8{1'b1}}), .pc(register_1_q), .d(register_1_q), .w(and_1_out), .instr(out_1), .data(out_2));
endmodule

module dual_port_ram (
  input  [7:0] addr,
  input  [7:0] pc,
  input  [7:0] d,
  input  w,
  output [7:0] instr,
  output [7:0] data
);

  wire clock_1_out, or_1_out;
  wire [7:0] multiplexer_1_out;

  Clock clock_1 (.out(clock_1_out));
  or or_1 (or_1_out, w, clock_1_out);
  Multiplexer #(.width(8)) multiplexer_1 (.in0(addr), .in1(pc), .out(multiplexer_1_out), .sel(clock_1_out));
  RAM #(.asyncread("true")) ram_1 (
    .addr(multiplexer_1_out), .we(or_1_out), .oe(1'b1), .clk(clock_1_out), .din(d), .dout(data));
  Register #(.trigger("falling")) pcbuf (.D(data), .en(1'b1), .clk(clock_1_out), .Q(instr));  // open: clr
endmodule
