// Logisim project processador.circ as structural Verilog: 6 circuits, main circuit main
// Memória de Inst. e Dados
module main (
);

  wire ALUSrc, and_1_out, Branch, CLK, ImmU, Inc, Ji, Jump, MemToReg, MemWrite, or_1_out, Reset, ula_1_zero,
       WriteR0, WriteReg;
  wire [1:0] multiplexer_4_out, RA, RB;
  wire [2:0] ALUOp;
  wire [3:0] Opcode;
  wire [7:0] adder_1_out, adder_2_out, B, bancoderegistradores_1_a, extensorsinal_1_b, extensorsinal_2_b,
       extensorzero_1_b, memoria_1_data, multiplexer_1_out, multiplexer_2_out, multiplexer_3_out,
       multiplexer_5_out, multiplexer_6_out, multiplexer_7_out, register_1_q, ula_1_s;

  ExtensorSinal extensorsinal_1 (.A({RA, RB}), .B(extensorsinal_1_b));
  Clock #(.highDuration(2), .lowDuration(2), .phaseOffset(1)) clock_1 (.out(CLK));
  Button button_1 (.out(Reset));
  Adder adder_1 (.a(extensorsinal_1_b), .b(register_1_q), .out(adder_1_out));  // open: cin, cout
  Adder adder_2 (.a(8'h1), .b(register_1_q), .out(adder_2_out));  // open: cin, cout
  or or_1 (or_1_out, and_1_out, Jump);
  and and_1 (and_1_out, ula_1_zero, Branch);
  // Probe on multiplexer_1_out
  Multiplexer #(.width(8)) multiplexer_1 (
    .in0(adder_2_out), .in1(multiplexer_2_out), .out(multiplexer_1_out), .sel(or_1_out));
  // Probe on Opcode
  Multiplexer #(.width(8)) multiplexer_2 (.in0(B), .in1(adder_1_out), .out(multiplexer_2_out), .sel(Ji));
  Register register_1 (.D(multiplexer_1_out), .en(1'b1), .clk(CLK), .Q(register_1_q), .clr(Reset));
  ROM #(.addrWidth(4), .dataWidth(13)) MemoriaDeControle (
    .addr(Opcode), .data({ALUSrc, ALUOp, Ji, Jump, Branch, WriteReg, MemToReg, MemWrite, WriteR0, Inc, ImmU}));
  // Probe on register_1_q
  // Probe on bancoderegistradores_1_a
  // Probe on B
  Memoria memoria_1 (
    .addr(B), .pc(register_1_q), .d(bancoderegistradores_1_a), .w(MemWrite), .Reset(Reset),
    .instr({Opcode, RA, RB}), .data(memoria_1_data));
  Multiplexer #(.width(8)) multiplexer_3 (.in0(ula_1_s), .in1(memoria_1_data), .out(multiplexer_3_out), .sel(MemToReg));
  // Probe on multiplexer_3_out
  Multiplexer #(.width(2)) multiplexer_4 (.in0(RA), .in1(2'b00), .out(multiplexer_4_out), .sel(WriteR0));
  // Probe on multiplexer_4_out
  // Probe on RB
  ExtensorSinal extensorsinal_2 (.A({RA, RB}), .B(extensorsinal_2_b));
  ExtensorZero extensorzero_1 (.A({RA, RB}), .B(extensorzero_1_b));
  BancoDeRegistradores bancoderegistradores_1 (
    .Reset(Reset), .Clk(CLK), .Dados(multiplexer_3_out), .WriteReg(WriteReg), .RW(multiplexer_4_out),
    .RA(multiplexer_4_out), .RB(RB), .A(bancoderegistradores_1_a), .B(B));
  Multiplexer #(.width(8)) multiplexer_5 (
    .in0(extensorsinal_2_b), .in1(extensorzero_1_b), .out(multiplexer_5_out), .sel(ImmU));
  // Probe on multiplexer_5_out
  Multiplexer #(.width(8)) multiplexer_6 (.in0(B), .in1(8'h1), .out(multiplexer_6_out), .sel(Inc));
  Multiplexer #(.width(8)) multiplexer_7 (
    .in0(multiplexer_6_out), .in1(multiplexer_5_out), .out(multiplexer_7_out), .sel(ALUSrc));
  ULA ula_1 (.A(bancoderegistradores_1_a), .B(multiplexer_7_out), .Funct(ALUOp), .Zero(ula_1_zero), .S(ula_1_s));

  // Other names for the same wires on the sheet: Resto[3:0] = {RA, RB}

  // Notes on the sheet:
  //   contents of MemoriaDeControle (hex, n*v repeats v):
  //   840 1980 830 808 1824 822 1825 1880 20 220 420 620 820 a20 c20 e20
endmodule

module BancoDeRegistradores (
  input  Reset,
  input  Clk,
  input  [7:0] Dados,
  input  WriteReg,
  input  [1:0] RW,
  input  [1:0] RA,
  input  [1:0] RB,
  output [7:0] A,
  output [7:0] B
);

  wire demultiplexer_1_out0, demultiplexer_1_out1, demultiplexer_1_out2, demultiplexer_1_out3;
  wire [7:0] register_1_q, register_2_q, register_3_q, register_4_q;

  Demultiplexer #(.select(2)) demultiplexer_1 (
    .out0(demultiplexer_1_out0), .out1(demultiplexer_1_out1), .out2(demultiplexer_1_out2),
    .out3(demultiplexer_1_out3), .in(WriteReg), .sel(RW));
  Register register_1 (.D(Dados), .en(demultiplexer_1_out0), .clk(Clk), .Q(register_1_q), .clr(Reset));
  Register register_2 (.D(Dados), .en(demultiplexer_1_out1), .clk(Clk), .Q(register_2_q), .clr(Reset));
  Register register_3 (.D(Dados), .en(demultiplexer_1_out2), .clk(Clk), .Q(register_3_q), .clr(Reset));
  Register register_4 (.D(Dados), .en(demultiplexer_1_out3), .clk(Clk), .Q(register_4_q), .clr(Reset));
  Multiplexer #(.select(2), .width(8)) multiplexer_1 (
    .in0(register_1_q), .in1(register_2_q), .in2(register_3_q), .in3(register_4_q), .out(A), .sel(RA));
  // Probe on A
  Multiplexer #(.select(2), .width(8)) multiplexer_2 (
    .in0(register_1_q), .in1(register_2_q), .in2(register_3_q), .in3(register_4_q), .out(B), .sel(RB));
  // Probe on B
endmodule

module ULA (
  input  [7:0] A,
  input  [7:0] B,
  input  [2:0] Funct,
  output Zero,
  output [7:0] S
);

  wire adder_1_cout, comparator_1_gt, comparator_1_lt, subtractor_1_bout;
  wire [7:0] D0, D1, D2, D3, D4, D5, D6, D7;

  Comparator comparator_1 (.a(A), .b({8{1'b0}}), .gt(comparator_1_gt), .eq(Zero), .lt(comparator_1_lt));
  assign D0 = ~B;  // NOT_Gate not_1, 8 bits wide
  assign D1 = A & B;  // AND_Gate and_1, 8 bits wide
  assign D2 = A | B;  // OR_Gate or_1, 8 bits wide
  assign D3 = A ^ B;  // XOR_Gate xor_1, 8 bits wide
  Adder adder_1 (.a(A), .b(B), .out(D4), .cin(1'b0), .cout(adder_1_cout));
  LED led_1 (.in(adder_1_cout));
  Subtractor subtractor_1 (.a(A), .b(B), .out(D5), .bin(1'b0), .bout(subtractor_1_bout));
  LED led_2 (.in(subtractor_1_bout));
  Shifter shifter_1 (.in(A), .\dist (B[2:0]), .out(D6));
  Shifter #(.shift("lr")) shifter_2 (.in(A), .\dist (B[2:0]), .out(D7));
  LED led_3 (.in(comparator_1_gt));
  LED led_4 (.in(comparator_1_lt));
  Multiplexer #(.select(3), .width(8)) multiplexer_1 (
    .in0(D0), .in1(D1), .in2(D2), .in3(D3), .in4(D4), .in5(D5), .in6(D6), .in7(D7), .out(S), .sel(Funct));

  // Notes on the sheet:
  //   Comparador
  //   NOT B
  //   A AND B
  //   A OR B
  //   A XOR B
  //   A + B
  //   A - B
  //   A << B
  //   A >> B
endmodule

module ExtensorSinal (
  input  [3:0] A,
  output [7:0] B
);


  assign B = {{5{A[3]}}, A[2:0]};
endmodule

module ExtensorZero (
  input  [3:0] A,
  output [7:0] B
);


  assign B = {4'b0000, A};
endmodule

module Memoria (
  input  [7:0] addr,
  input  [7:0] pc,
  input  [7:0] d,
  input  w,
  input  Reset,
  output [7:0] instr,
  output [7:0] data
);

  wire clock_1_out, or_1_out;
  wire [7:0] multiplexer_1_out;

  Clock clock_1 (.out(clock_1_out));
  or or_1 (or_1_out, w, clock_1_out);
  Multiplexer #(.width(8)) multiplexer_1 (.in0(addr), .in1(pc), .out(multiplexer_1_out), .sel(clock_1_out));
  RAM #(.asyncread("true")) ram_1 (
    .addr(multiplexer_1_out), .we(or_1_out), .oe(1'b1), .clk(clock_1_out), .din(d), .dout(data));
  Register #(.trigger("falling")) pcbuf (.D(data), .en(1'b1), .clk(clock_1_out), .Q(instr), .clr(Reset));
endmodule
